// Logisim project Full-Adder-3bits.circ as structural Verilog: 1 circuit, main circuit main
module main (
  input  A2,
  input  A1,
  input  A0,
  input  B2,
  input  B1,
  input  B0,
  output Out1,
  output Out2,
  output Out0
);

  wire main_1_co, main_2_co;

  Half_Adder_main main_1 (.In1(A0), .In2(B0), .CO(main_1_co), .Output(Out0));
  Full_Adder_main main_2 (.A(A1), .B(B1), .Cin(main_1_co), .Out(Out1), .CO(main_2_co));
  Full_Adder_main main_3 (.A(A2), .B(B2), .Cin(main_2_co), .Out(Out2));  // open: CO
endmodule
