// Logisim project Half-Adder.circ as structural Verilog: 1 circuit, main circuit main
module main (
  input  In1,
  input  In2,
  output CO,
  output Output
);

  and and_1 (CO, In1, In2);
  xor xor_1 (Output, In1, In2);
endmodule
