// Logisim project Projeto.circ as structural Verilog: 9 circuits, main circuit A
module A (
  input  In1,
  input  In2,
  input  In3,
  output A
);

  wire and_1_out, and_2_out, and_3_out, not_1_out, not_2_out, not_3_out;

  not not_1 (not_1_out, In1);
  not not_2 (not_2_out, In2);
  not not_3 (not_3_out, In3);
  and and_1 (and_1_out, not_1_out, In2);
  and and_2 (and_2_out, not_2_out, In1);
  and and_3 (and_3_out, In2, not_3_out);
  or or_1 (A, and_1_out, and_2_out, and_3_out);
endmodule

module B (
  input  In1,
  input  In2,
  input  In3,
  output B
);

  wire and_1_out, and_2_out, and_3_out, not_1_out, not_2_out;

  not not_1 (not_1_out, In2);
  not not_2 (not_2_out, In3);
  and and_1 (and_1_out, In1, not_1_out);
  and and_2 (and_2_out, not_1_out, not_2_out);
  and and_3 (and_3_out, In1, not_2_out);
  or or_1 (B, and_1_out, and_2_out, and_3_out);
endmodule

module C (
  input  In1,
  input  In2,
  input  In3,
  output C
);

  wire and_1_out, and_2_out, not_1_out, not_2_out;

  and and_1 (and_1_out, In1, In3);
  not not_1 (not_1_out, In1);
  and and_2 (and_2_out, not_1_out, not_2_out);
  not not_2 (not_2_out, In3);
  or or_1 (C, and_1_out, In2, and_2_out);
endmodule

module D (
  input  In1,
  input  In2,
  input  In3,
  output D
);

  wire and_1_out, and_2_out, not_1_out, not_2_out, not_3_out;

  not not_1 (not_1_out, In1);
  and and_1 (and_1_out, In2, In3);
  not not_2 (not_2_out, In3);
  and and_2 (and_2_out, not_2_out, not_3_out);
  not not_3 (not_3_out, In2);
  or or_1 (D, not_1_out, and_1_out, and_2_out);
endmodule

module E (
  input  In1,
  input  In2,
  input  In3,
  output E
);

  wire and_1_out, and_2_out, not_1_out, not_2_out;

  not not_1 (not_1_out, In1);
  not not_2 (not_2_out, In3);
  and and_1 (and_1_out, not_1_out, not_2_out);
  and and_2 (and_2_out, In2, not_2_out);
  or or_1 (E, and_1_out, and_2_out);
endmodule

module F (
  input  In1,
  input  In2,
  input  In3,
  output F
);

  wire and_1_out, and_2_out, and_3_out, and_4_out, not_1_out, not_2_out, not_3_out;

  not not_1 (not_1_out, In1);
  not not_2 (not_2_out, In2);
  not not_3 (not_3_out, In3);
  and and_1 (and_1_out, not_1_out, not_3_out);
  and and_2 (and_2_out, In2, not_3_out);
  and and_3 (and_3_out, not_1_out, In2);
  and and_4 (and_4_out, not_2_out, In3, In1);
  or or_1 (F, and_1_out, and_2_out, and_3_out, and_4_out);
endmodule

module G (
  input  In1,
  input  In2,
  input  In3,
  output G
);

  wire and_1_out, not_1_out, not_2_out;

  not not_1 (not_1_out, In1);
  not not_2 (not_2_out, In2);
  and and_1 (and_1_out, not_1_out, not_2_out);
  or or_1 (G, In1, and_1_out, In3);
endmodule

module Encoder (
  input  In2,
  input  In1,
  input  In0,
  output out_4,
  output out_5,
  output out_6,
  output out_7,
  output out_8,
  output out_9,
  output out_10
);

  A a_1 (.In1(In2), .In2(In1), .In3(In0), .A(out_4));
  B b_1 (.In1(In2), .In2(In1), .In3(In0), .B(out_5));
  C c_1 (.In1(In2), .In2(In1), .In3(In0), .C(out_6));
  D d_1 (.In1(In2), .In2(In1), .In3(In0), .D(out_7));
  E e_1 (.In1(In2), .In2(In1), .In3(In0), .E(out_8));
  F f_1 (.In1(In2), .In2(In1), .In3(In0), .F(out_9));
  G g_1 (.In1(In2), .In2(In1), .In3(In0), .G(out_10));
endmodule

module Main (
  input  in_1,
  input  in_2,
  input  in_3,
  input  in_4,
  input  in_5,
  input  in_6
);

  wire clock_1_out, encoder_1_out_4, encoder_1_out_5, encoder_1_out_6, encoder_1_out_7, encoder_1_out_8,
       encoder_1_out_9, encoder_1_out_10, main_1_out0, main_1_out1, main_1_out2, main_2_out0, main_2_out1,
       main_2_out2;

  Full_Adder_3bits_main main_1 (
    .A2(in_1), .A1(in_2), .A0(in_3), .B1(in_5), .B0(in_6), .B2(in_4), .Out0(main_1_out0), .Out1(main_1_out1),
    .Out2(main_1_out2));
  Clock clock_1 (.out(clock_1_out));
  Sync_Register_3bits_main main_2 (
    .In2(main_1_out2), .In1(main_1_out1), .In0(main_1_out0), .Out2(main_2_out2), .Out1(main_2_out1),
    .Out0(main_2_out0));
  Encoder encoder_1 (
    .In2(main_2_out2), .In1(main_2_out1), .In0(main_2_out0), .out_4(encoder_1_out_4),
    .out_5(encoder_1_out_5), .out_6(encoder_1_out_6), .out_7(encoder_1_out_7), .out_8(encoder_1_out_8),
    .out_9(encoder_1_out_9), .out_10(encoder_1_out_10));
  _7_Segment_Display u_7_segment_display_1 (
    .g(encoder_1_out_4), .f(encoder_1_out_5), .a(encoder_1_out_6), .b(encoder_1_out_7), .e(encoder_1_out_8),
    .d(encoder_1_out_9), .c(encoder_1_out_10));  // open: dp
endmodule
