// Logisim project Sync_Register-3bits.circ as structural Verilog: 1 circuit, main circuit main
module main (
  input  In2,
  input  In1,
  input  In0,
  output Out2,
  output Out1,
  output Out0
);

  wire CLK_out;

  Clock CLK (.out(CLK_out));
  D_Flip_Flop d_ff_1 (.clk(CLK_out), .D(In2), .Q(Out2));  // open: Qn, preset, en, reset
  D_Flip_Flop d_ff_2 (.clk(CLK_out), .D(In1), .Q(Out1));  // open: Qn, preset, en, reset
  D_Flip_Flop d_ff_3 (.clk(CLK_out), .D(In0), .Q(Out0));  // open: Qn, preset, en, reset
endmodule
